# Fritzing sketch Circuit-wifi-ws2813 (saved by Fritzing 0.9.3b)

parts:
  LPD8806_RGB_LED_Strip1 = LPD8806 RGB LED Strip
  LPD8806_RGB_LED_Strip2 = LPD8806 RGB LED Strip
  LPD8806_RGB_LED_Strip3 = LPD8806 RGB LED Strip
  LPD8806_RGB_LED_Strip4 = LPD8806 RGB LED Strip
  LPD8806_RGB_LED_Strip5 = LPD8806 RGB LED Strip
  U1 = MAX485 Breakout [chip_label=? package=THT]
  U2 = ESP32S-HiLetgo [part_number=ESP32S-HiLetgo]
  D1 = Schottky Diode [part_number=1N5817 package="300 mil [THT]"]
  D2 = Schottky Diode [part_number=1N5817 package="300 mil [THT]"]
  R1 = Resistor [tolerance=±5% resistance=220 package="0402 [SMD]"]
  HLK-PM2 = HLK-PM01
  STEPDOWN1 = Step Down 5V to 3.3V [package="DIP (Dual Inline) [THT]"]
  D3 = Diode [package=diode-1n4148]
  LPD8806_RGB_LED_Strip6 = LPD8806 RGB LED Strip
  R2 = Resistor [tolerance=±5% resistance=220 package="0402 [SMD]"]
  R3 = Resistor [tolerance=±5% resistance=220 package="0402 [SMD]"]
  R4 = Resistor [tolerance=±5% resistance=220 package="0402 [SMD]"]
  R5 = Resistor [tolerance=±5% resistance=220 package="0402 [SMD]"]
  R6 = Resistor [tolerance=±5% resistance=220 package="0402 [SMD]"]
  C7 = Tantalum Capacitor [capacitance=1μF package="200 mil [THT, tantalum]"]  # not connected
  C8 = Tantalum Capacitor [capacitance=1μF package="200 mil [THT, tantalum]"]
  C9 = Tantalum Capacitor [capacitance=1μF package="200 mil [THT, tantalum]"]  # not connected
  C10 = Tantalum Capacitor [capacitance=1μF package="200 mil [THT, tantalum]"]  # not connected
  C11 = Tantalum Capacitor [capacitance=1μF package="200 mil [THT, tantalum]"]  # not connected
  C12 = Tantalum Capacitor [capacitance=1μF package="200 mil [THT, tantalum]"]  # not connected

nets:
  N1: LPD8806_RGB_LED_Strip1.GND#0, D1.anode
  N2: LPD8806_RGB_LED_Strip1.DI, D2.anode
  N3: LPD8806_RGB_LED_Strip1.GND#4, C8.-
  N4: LPD8806_RGB_LED_Strip1.DO, R2.Pin_0
  N5: LPD8806_RGB_LED_Strip1.CO, LPD8806_RGB_LED_Strip2.CI
  N6: LPD8806_RGB_LED_Strip2.DI, R2.Pin_1
  N7: LPD8806_RGB_LED_Strip2.+5V, C8.+
  N8: LPD8806_RGB_LED_Strip2.DO, R3.Pin_0
  N9: LPD8806_RGB_LED_Strip2.CO, LPD8806_RGB_LED_Strip3.CI
  N10: LPD8806_RGB_LED_Strip3.DI, R3.Pin_1
  N11: LPD8806_RGB_LED_Strip3.DO, R4.Pin_0
  N12: LPD8806_RGB_LED_Strip3.CO, LPD8806_RGB_LED_Strip4.CI
  N13: LPD8806_RGB_LED_Strip4.DI, R4.Pin_1
  N14: LPD8806_RGB_LED_Strip4.DO, R5.Pin_0
  N15: LPD8806_RGB_LED_Strip4.CO, LPD8806_RGB_LED_Strip5.CI
  N16: LPD8806_RGB_LED_Strip5.DI, R5.Pin_1
  N17: LPD8806_RGB_LED_Strip5.DO, R6.Pin_0
  N18: LPD8806_RGB_LED_Strip5.CO, LPD8806_RGB_LED_Strip6.CI
  N19: U1.RE, U1.DE, U2.GPIO35
  N20: U1.A, R1.Pin_0
  N21: U2.3.3, STEPDOWN1.OUT
  GND: U2.GND, HLK-PM2.-Vo, STEPDOWN1.GND
  N22: D1.cathode, R1.Pin_1
  N23: D2.cathode, D3.C
  N24: HLK-PM2.+Vo, STEPDOWN1.IN, D3.A
  N25: LPD8806_RGB_LED_Strip6.DI, R6.Pin_1

custom parts:
  LPD8806 RGB LED Strip: Digitally addressable RGB LED strip
  MAX485 Breakout: MAX485 RS485 breakout board
  ESP32S-HiLetgo: HiLetgo ESP-WROOM-32 ESP32 ESP-32S Development Board 2.4GHz Dual-Mode WiFi + Bluetooth Dual Cores Microcontroller The ESP32 integrated with Antenna switches, RF Balun, power amplifiers, low-noise amplifiers, filters, and management modules, and the entire solution occupies the least area of PCB. 2.4 GHz Wi-Fi plus Bluetooth dual-mode chip, with TSMC Ultra-low power consumption 40nm technology,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
  Step Down 5V to 3.3V: Step Down 5V to 3.3V 1A
